// Logisim project ALU.circ as structural Verilog: 1 circuit, main circuit ALU
module ALU (
  input  [31:0] A,
  input  [31:0] B,
  input  [4:0] Shift,
  input  [3:0] Codop,
  input  CarryIn,
  output [31:0] S,
  output [3:0] Flags
);

  wire C_ADC, C_CMN, C_CMP, C_RSB, not_2_out, subtractor_2_bout, undriven, undriven_2, undriven_3,
       undriven_4, undriven_5, undriven_6, undriven_7, undriven_8, undriven_9, undriven_10, undriven_11,
       undriven_12, undriven_13, undriven_14;
  wire [30:0] multiplexer_2_out;
  wire [31:0] A_N_D, ADC, ASR, BIC, CMN, CMP, EOR, LSL, LSR, MUL, multiplexer_3_out, MVN, not_1_out, ORR,
       R_O_R, RSB, SBS;

  assign A_N_D = A & B;  // AND_Gate and_1, 32 bits wide
  Adder #(.width(32)) adder_1 (.a(A), .b(B), .out(CMN), .cout(C_CMN));  // open: cin
  assign EOR = A ^ B;  // XOR_Gate xor_1, 32 bits wide
  Shifter #(.width(32)) shifter_1 (.in(B), .\dist (Shift), .out(LSL));
  Shifter #(.shift("lr"), .width(32)) shifter_2 (.in(B), .\dist (Shift), .out(LSR));
  Shifter #(.shift("ar"), .width(32)) shifter_3 (.in(B), .\dist (Shift), .out(ASR));
  Subtractor #(.width(32)) subtractor_1 (.a({32{1'b0}}), .b(A), .out(RSB), .bout(C_RSB));  // open: bin
  assign not_1_out = ~A;  // NOT_Gate not_1, 32 bits wide
  Adder #(.width(32)) adder_2 (.a(A), .b(B), .out(ADC), .cin(CarryIn), .cout(C_ADC));
  not not_2 (not_2_out, CarryIn);
  Subtractor #(.width(32)) subtractor_2 (.a(B), .b(A), .out(SBS), .bin(not_2_out), .bout(subtractor_2_bout));
  not not_3 (C_ADC, subtractor_2_bout);
  Shifter #(.shift("rr"), .width(32)) shifter_4 (.in(B), .\dist (Shift), .out(R_O_R));
  assign BIC = not_1_out & B;  // AND_Gate and_2, 32 bits wide
  Multiplexer #(.select(4), .width(32)) multiplexer_1 (
    .in0(A_N_D), .in1(EOR), .in2(LSL), .in3(LSR), .in4(ASR), .in5(ADC), .in6(SBS), .in7(R_O_R),
    .in8({32{1'b0}}), .in9(RSB), .in10(CMP), .in11(CMN), .in12(ORR), .in13(MUL), .in14(BIC), .in15(MVN),
    .out(S), .sel(Codop));
  assign MVN = ~A;  // NOT_Gate not_4, 32 bits wide
  assign ORR = A | B;  // OR_Gate or_1, 32 bits wide
  Subtractor #(.width(32)) subtractor_3 (.a(B), .b(A), .out(CMP), .bout(C_CMP));  // open: bin
  Multiplier #(.width(32)) multiplier_1 (.a(B), .b(A), .out(MUL));  // open: cin, cout
  Multiplexer #(.select(4), .width(32)) multiplexer_2 (
    .in0(A_N_D), .in1(EOR), .in2(LSL), .in3(LSR), .in4(ASR), .in5(ADC), .in6(SBS), .in7(R_O_R), .in8(A_N_D),
    .in9(RSB), .in10(CMP), .in11(CMN), .in12(ORR), .in13(MUL), .in14(BIC), .in15(MVN),
    .out({Flags[2], multiplexer_2_out}), .sel(Codop));
  Multiplexer #(.select(4), .width(32)) multiplexer_3 (
    .in0(A_N_D), .in1(EOR), .in2(LSL), .in3(LSR), .in4(ASR), .in5(ADC), .in6(SBS), .in7(R_O_R), .in8(A_N_D),
    .in9(RSB), .in10(CMP), .in11(CMN), .in12(ORR), .in13(MUL), .in14(BIC), .in15(MVN),
    .out(multiplexer_3_out), .sel(Codop));
  nor nor_1 (Flags[3], multiplexer_3_out[0], multiplexer_3_out[1], multiplexer_3_out[2], multiplexer_3_out[3], multiplexer_3_out[4], multiplexer_3_out[5], multiplexer_3_out[6], multiplexer_3_out[7], multiplexer_3_out[8], multiplexer_3_out[9], multiplexer_3_out[10], multiplexer_3_out[11], multiplexer_3_out[12], multiplexer_3_out[13], multiplexer_3_out[14], multiplexer_3_out[15], multiplexer_3_out[16], multiplexer_3_out[17], multiplexer_3_out[18], multiplexer_3_out[19], multiplexer_3_out[20], multiplexer_3_out[21], multiplexer_3_out[22], multiplexer_3_out[23], multiplexer_3_out[24], multiplexer_3_out[25], multiplexer_3_out[26], multiplexer_3_out[27], multiplexer_3_out[28], multiplexer_3_out[29], multiplexer_3_out[30], multiplexer_3_out[31]);
  Multiplexer #(.select(4)) multiplexer_4 (
    .in0(1'b0), .in1(1'b0), .in2(undriven_13), .in3(undriven_12), .in4(undriven_11), .in5(undriven_10),
    .in6(undriven_9), .in7(undriven_8), .in8(undriven_14), .in9(undriven_7), .in10(undriven_6),
    .in11(undriven_5), .in12(undriven_4), .in13(undriven_3), .in14(undriven), .in15(undriven_2), .sel(Codop));  // open: out

  // Other names for the same wires on the sheet: N = Flags[2]; V = Flags[0]; C = Flags[1]; Z = Flags[3];
  //   op[3:0] = Codop

  // Notes on the sheet:
  //   Note: for ROR, C = N
  //   Note 2: assume that shift > 0 for LSL and LSR
  //   TST 
  //   TST 
  //   CARRY HERE
endmodule
